// Digital circuit instruction_memory.dig as structural Verilog
module instruction_memory (
  input  [6:0] A,
  input  [4:0] PN,
  output [31:0] D
);

  wire [31:0] b_d, beq_d, bgt_d, blbx_d, ble_d, dp_asr_imm_d, dp_imm_d, dp_lsl_imm_d, dp_lsr_reg_d, dp_reg_d,
       fib_rec_d, get_bitseq_d, max3_d, mem_imm_d, mem_reg_d, mem_shift_reg_d, merge_sort_d, mul_d,
       quadratic_d, rsb_d, sort_d;

  ROM #(.AddrBits(7), .Bits(32)) dp_reg (.A(A), .sel(1'b1), .D(dp_reg_d));
  ROM #(.AddrBits(7), .Bits(32)) dp_imm (.A(A), .sel(1'b1), .D(dp_imm_d));
  ROM #(.AddrBits(7), .Bits(32)) dp_lsl_imm (.A(A), .sel(1'b1), .D(dp_lsl_imm_d));
  ROM #(.AddrBits(7), .Bits(32)) dp_lsr_reg (.A(A), .sel(1'b1), .D(dp_lsr_reg_d));
  ROM #(.AddrBits(7), .Bits(32)) dp_asr_imm (.A(A), .sel(1'b1), .D(dp_asr_imm_d));
  ROM #(.AddrBits(7), .Bits(32)) mem_reg (.A(A), .sel(1'b1), .D(mem_reg_d));
  ROM #(.AddrBits(7), .Bits(32)) mem_imm (.A(A), .sel(1'b1), .D(mem_imm_d));
  ROM #(.AddrBits(7), .Bits(32)) mem_shift_reg (.A(A), .sel(1'b1), .D(mem_shift_reg_d));
  ROM #(.AddrBits(7), .Bits(32)) blbx (.A(A), .sel(1'b1), .D(blbx_d));
  ROM #(.AddrBits(7), .Bits(32)) b (.A(A), .sel(1'b1), .D(b_d));
  ROM #(.AddrBits(7), .Bits(32)) beq (.A(A), .sel(1'b1), .D(beq_d));
  ROM #(.AddrBits(7), .Bits(32)) ble (.A(A), .sel(1'b1), .D(ble_d));
  ROM #(.AddrBits(7), .Bits(32)) bgt (.A(A), .sel(1'b1), .D(bgt_d));
  ROM #(.AddrBits(7), .Bits(32)) mul (.A(A), .sel(1'b1), .D(mul_d));
  ROM #(.AddrBits(7), .Bits(32)) rsb (.A(A), .sel(1'b1), .D(rsb_d));
  ROM #(.AddrBits(7), .Bits(32)) quadratic (.A(A), .sel(1'b1), .D(quadratic_d));
  ROM #(.AddrBits(7), .Bits(32)) get_bitseq (.A(A), .sel(1'b1), .D(get_bitseq_d));
  ROM #(.AddrBits(7), .Bits(32)) max3 (.A(A), .sel(1'b1), .D(max3_d));
  ROM #(.AddrBits(7), .Bits(32)) fib_rec (.A(A), .sel(1'b1), .D(fib_rec_d));
  ROM #(.AddrBits(7), .Bits(32)) sort (.A(A), .sel(1'b1), .D(sort_d));
  ROM #(.AddrBits(7), .Bits(32)) merge_sort (.A(A), .sel(1'b1), .D(merge_sort_d));
  Multiplexer #(.Selector_Bits(5), .Bits(32)) multiplexer_1 (
    .sel(PN), .in_0(dp_reg_d), .in_1(dp_imm_d), .in_2(dp_lsl_imm_d), .in_3(dp_lsr_reg_d),
    .in_4(dp_asr_imm_d), .in_5(mem_reg_d), .in_6(mem_imm_d), .in_7(mem_shift_reg_d), .in_8(blbx_d),
    .in_9(b_d), .in_10(beq_d), .in_11(ble_d), .in_12(bgt_d), .in_13(mul_d), .in_14(rsb_d),
    .in_15(quadratic_d), .in_16(get_bitseq_d), .in_17(max3_d), .in_18(fib_rec_d), .in_19(sort_d),
    .in_20(merge_sort_d), .in_21({32{1'b0}}), .in_22({32{1'b0}}), .in_23({32{1'b0}}), .in_24({32{1'b0}}),
    .in_25({32{1'b0}}), .in_26({32{1'b0}}), .in_27({32{1'b0}}), .in_28({32{1'b0}}), .in_29({32{1'b0}}),
    .in_30({32{1'b0}}), .in_31({32{1'b0}}), .out(D));

  // Notes on the sheet:
  //   contents of dp_reg (hex, n*v repeats v):
  //   e3a00000,e3a01001,e0800001,e2800000
  //   contents of dp_imm (hex, n*v repeats v):
  //   e3a00002,e2400001,e2800000
  //   contents of dp_lsl_imm (hex, n*v repeats v):
  //   e3a00001,e1a00100,e2800000
  //   contents of dp_lsr_reg (hex, n*v repeats v):
  //   e3a00002,e3a01001,e1a00130,e2800000
  //   contents of dp_asr_imm (hex, n*v repeats v):
  //   e3a00002,e1a000c0,e2800000
  //   contents of mem_reg (hex, n*v repeats v):
  //   e3a0d0ff,e1a0d10d,e24dd008,e3a00001,e3a0c004,e58d0004,e3a00002,e79d000c,e2800000
  //   contents of mem_imm (hex, n*v repeats v):
  //   e3a0d0ff,e1a0d10d,e24dd008,e3a00001,e58d0004,e3a00002,e59d0004,e2800000
  //   contents of mem_shift_reg (hex, n*v repeats v):
  //   e3a0d0ff,e1a0d10d,e24dd008,e3a00001,e3a0c001,e58d0004,e3a00002,e79d010c,e2800000
  //   7
  //   contents of blbx (hex, n*v repeats v):
  //   e3a00001,e3a01002,eb000000,e2800000,e0800001,e12fff1e
  //   contents of b (hex, n*v repeats v):
  //   ea000003,e3a00000,e2400001,e2800001,e2800000,e3a00001,e2800000
  //   contents of beq (hex, n*v repeats v):
  //   e3a01001,e3510001,a000001,e3a00000,e2800000,e3a00001,e2800000
  //   contents of ble (hex, n*v repeats v):
  //   e3a01001,e3510002,da000001,e3a00000,e2800000,e3a00001,e2800000
  //   contents of bgt (hex, n*v repeats v):
  //   e3a01001,e3510000,ca000001,e3a00000,e2800000,e3a00001,e2800000
  //   contents of mul (hex, n*v repeats v):
  //   e3a01002,e3a02003,e0000291,e2800000
  //   contents of rsb (hex, n*v repeats v):
  //   e3a00001,e2600002,e2800000
  //   14
  //   contents of quadratic (hex, n*v repeats v):
  //   e3a00002,e3a01004,e3a02006,e3a03008,eb000000,e2800000,e0020290,e0000090,e0000091,
  //   e0820000,e0830000,e12fff1e
  //   contents of get_bitseq (hex, n*v repeats v):
  //   e3a000ff,e1a00200,e3a01004,e3a0200b,eb000000,e2800000,e042c001,e1a00130,e3a03001,
  //   e1a03f83,e1a03c53,e26cc01f,e1a03c33,e0000003,e12fff1e
  //   contents of max3 (hex, n*v repeats v):
  //   e3a00001,e3a02003,e3a03002,eb000000,e2800000,e1500001,ca000000,e1a00001,e1500002,
  //   ca000000,e1a00002,e12fff1e
  //   contents of fib_rec (hex, n*v repeats v):
  //   e3a0d001,e1a0d50d,e3a0000a,eb000000,e2800000,e24dd008,e58de000,e3500001,da000009,
  //   e2400001,e58d0004,ebfffff8,e1a01000,e59d0004,e2400001,e58d1004,ebfffff3,e59d1004,
  //   e0800001,e59de000,e28dd008,e12fff1e
  //   contents of sort (hex, n*v repeats v):
  //   e3a0d001,e1a0d50d,e24dd014,e3a00001,e58d0000,e3a00005,e58d0004,e3a00002,e58d0008,
  //   e3a00004,e58d000c,e3a00003,e58d0010,e1a0000d,e3a01005,eb000000,e2800000,e24dd008,
  //   e58d4000,e58de004,e3a0c000,e15c0001,aa000023,e24dd010,e58d0000,e58d1004,e58dc008,
  //   e041100c,e1a0c10c,e080000c,eb00001f,e1a02000,e59dc008,e59d1004,e59d0000,e28dd010,
  //   e082400c,e7902104,e790310c,e1520003,da00000f,e24dd008,e58dc000,e58d0004,e1a0c10c,
  //   e080000c,e5802000,e59d0004,e59dc000,e58d4000,e58d0004,e1a04104,e0800004,e5803000,
  //   e59d0004,e59d4000,e28dd008,e28cc001,eaffffd9,e59de004,e59d4000,e28dd008,e12fff1e,
  //   e24dd008,e58d4000,e3a02000,e3a0c000,e151000c,a000006,e790310c,e7904102,e1530004,da000000,
  //   e1a0200c,e28cc001,eafffff6,e1a00002,e59d4000,e28dd008,e12fff1e
  //   contents of merge_sort (hex, n*v repeats v):
  //   e3a0d001,e1a0d50d,e24dd014,e3a0000a,e58d0000,e3a00006,e58d0004,e3a00008,e58d0008,
  //   e3a00009,e58d000c,e3a00007,e58d0010,e1a0000d,e24dd014,e1a0100d,e3a02000,e3a03004,
  //   eb000000,e2800000,e24dd010,e58de000,e58d4004,e1530002,da00000a,e0824003,e1a040a4,
  //   e58d3008,e1a03004,ebfffff5,e59d3008,e58d2008,e2842001,ebfffff1,e59d2008,eb000003,
  //   e59d4004,e59de000,e28dd010,e12fff1e,e24dd020,e58d4000,e58d5004,e58d6008,e58d700c,
  //   e58d8010,e58d9014,e58da018,e0824003,e1a040a4,e1a05002,e2846001,e1a0c002,e15c0003,
  //   ca00001a,e1a07105,e7907007,e1a08106,e7908008,e1a0910c,e0819009,e284a001,e155000a,
  //   1a000002,e5898000,e2866001,ea00000c,e283a001,e156000a,1a000002,e5897000,e2855001,
  //   ea000006,e1570008,aa000002,e5897000,e2855001,ea000001,e5898000,e2866001,e28cc001,
  //   eaffffe2,e1a0c002,e15c0003,ca000009,e1a0810c,e7917008,e24dd008,e58d0000,e0800008,
  //   e5807000,e59d0000,e28dd008,e28cc001,eafffff3,e59da018,e59d9014,e59d8010,e59d700c,
  //   e59d6008,e59d5004,e59d4000,e28dd020,e12fff1e
  //   20
endmodule
